// Logisim project control-logic.circ as structural Verilog: 1 circuit, main circuit control_logic
module control_logic (
  input  [31:0] inst,
  input  BrEq,
  input  BrLt,
  input  [3:0] in_4,
  output PCSel,
  output RegWEn,
  output [2:0] ImmSel,
  output BrUn,
  output ASel,
  output BSel,
  output [3:0] ALUSel,
  output MemRW,
  output [1:0] WBSel,
  output CSRSel,
  output CSRWen
);

  wire [2:0] bit_extender_1_out;

  assign bit_extender_1_out = {{2{1'b0}}, inst[3]};  // Bit_Extender bit_extender_1
  or or_1 (PCSel, BrEq, BrLt);
  assign ImmSel = bit_extender_1_out | inst[6:4];  // OR_Gate or_2, 3 bits wide
  // Probe on ImmSel
  and and_1 (BrUn, inst[13], inst[14]);

  assign ALUSel = in_4;
  assign BSel = 1'b1;
  assign RegWEn = 1'b1;

  // Other names for the same wires on the sheet: opcode[6:0] = inst[6:0]; rd[4:0] = inst[11:7];
  //   funct3[2:0] = inst[14:12]; rs1[4:0] = inst[19:15]; imm[11:0] = inst[31:20]; rs2[4:0] = inst[24:20];
  //   funct7[6:0] = inst[31:25]; immed[6:0] = inst[31:25]

  // Notes on the sheet:
  //   I-type: 000,0011
  //   U-type: 001,0111
  //   S-type: 010,0011
  //   R-type: 011,0011; no imm
  //   SB-type: 110,0011
  //   UJ-type: 110,1111
  //   INPUTS to your circuit
  //   ImmSel generator logic
  //   while writting ImmSel, Rtype does not contain imm, so Rtype would not be included.
  //   there is another way to design this circuit, refer to cnblogs: 16225150 
  //   DON'T CHANGE THE LOCATIONS OF THE INPUTS AND OUTPUTS!
  //   OUTPUT from your circuit
  //   the rightest 2 bit always be 1 in these instruction, so this 2 bit would not be contained. becasue this 2 bit cannot identify instrcut type
  //   the highest(leftest) bits shows a regularity. Itype-> 000, Utype->001, Stype->010, SBType-> 110, UJType->110
  //   these 3bits cannot distinct UJ/SB type only, but the 3rd bit is 1 only in UJType. so we can make OR between highest 3bits and extended 3rd bit, to produce a regularity 3bits
endmodule
